# Fritzing sketch control (saved by Fritzing 0.9.3b)

parts:
  seqledsctrl = 74HC595 [package="DIP16 [THT]"]
  tempoledsctrl = 74HC595 [package="DIP16 [THT]"]
  arduino_nano = Arduino Nano (Rev3.0)
  2n3904_(x2)_-_1 = MMDT3904 [package=sot363]
  2n3904_(x2)_-_2 = MMDT3904 [package=sot363]
  2n3904_(x2)_-_3 = MMDT3904 [package=sot363]
  2n3904_(x2)_-_4 = MMDT3904 [package=sot363]
  2n3904_(x2)_-_5 = MMDT3904 [package=sot363]
  seqled1 = RGB LED (com. anode, rbg) [package="5 mm [THT]"]
  seqled2 = RGB LED (com. anode, rbg) [package="5 mm [THT]"]
  seqled3 = RGB LED (com. anode, rbg) [package="5 mm [THT]"]
  seqled4 = RGB LED (com. anode, rbg) [package="5 mm [THT]"]
  seqled5 = RGB LED (com. anode, rbg) [package="5 mm [THT]"]
  seqled6 = RGB LED (com. anode, rbg) [package="5 mm [THT]"]
  seqled7 = RGB LED (com. anode, rbg) [package="5 mm [THT]"]
  seqled8 = RGB LED (com. anode, rbg) [package="5 mm [THT]"]
  playstopled = LED - 3mm [color="Red (633nm)" package="3 mm [THT]"]
  muteled = LED - 3mm [color="Red (633nm)" package="3 mm [THT]"]
  seqbutt1 = Toggle Switch [package=THT]
  seqbutt2 = Toggle Switch [package=THT]
  seqbutt3 = Toggle Switch [package=THT]
  seqbutt4 = Toggle Switch [package=THT]
  seqbutt8 = Toggle Switch [package=THT]
  seqbutt5 = Toggle Switch [package=THT]
  seqbutt6 = Toggle Switch [package=THT]
  seqbutt7 = Toggle Switch [package=THT]
  ctrlbutt1 = Toggle Switch [package=THT]
  ctrlbutt2 = Toggle Switch [package=THT]
  ctrlbutt3 = Toggle Switch [package=THT]
  ctrlbutt4 = Toggle Switch [package=THT]
  ctrlbutt5 = Toggle Switch [package=THT]
  ctrlbutt6 = Toggle Switch [package=THT]
  ctrlbutt7 = Toggle Switch [package=THT]
  ctrlbutt8 = Toggle Switch [package=THT]
  7seg = 7 Segment Display
  tranr1 = Resistor [tolerance=±5% resistance=1k package=THT]
  tranr2 = Resistor [tolerance=±5% resistance=1k package=THT]
  tranr3 = Resistor [tolerance=±5% resistance=1k package=THT]
  tranr4 = Resistor [tolerance=±5% resistance=1k package=THT]
  tranr5 = Resistor [tolerance=±5% resistance=1k package=THT]
  tranr6 = Resistor [tolerance=±5% resistance=1k package=THT]
  tranr7 = Resistor [tolerance=±5% resistance=1k package=THT]
  tranr8 = Resistor [tolerance=±5% resistance=1k package=THT]
  tranr9 = Resistor [tolerance=±5% resistance=1k package=THT]
  tranr10 = Resistor [tolerance=±5% resistance=1k package=THT]
  ctrlbutts = 74HC165 [package="DIP16 [THT]"]
  seqbutts = 74HC165 [package="DIP16 [THT]"]
  7segr1 = Resistor [tolerance=±5% resistance=470 package=THT]
  ledr11 = Resistor [tolerance=±5% resistance=47 package=THT]
  ledr12 = Resistor [tolerance=±5% resistance=470 package=THT]
  ledr13 = Resistor [tolerance=±5% resistance=470 package=THT]
  ledr14 = Resistor [tolerance=±5% resistance=470 package=THT]
  ledr15 = Resistor [tolerance=±5% resistance=470 package=THT]
  ledr16 = Resistor [tolerance=±5% resistance=470 package=THT]
  2n3904_(x2)_-_6 = MMDT3904 [package=sot363]
  2n3904_(x2)_-_7 = MMDT3904 [package=sot363]
  2n3904_(x2)_-_8 = MMDT3904 [package=sot363]
  2n3904_(x2)_-_9 = MMDT3904 [package=sot363]
  tranr11 = Resistor [tolerance=±5% resistance=1k package=THT]
  tranr12 = Resistor [tolerance=±5% resistance=1k package=THT]
  tranr13 = Resistor [tolerance=±5% resistance=1k package=THT]
  tranr14 = Resistor [tolerance=±5% resistance=1k package=THT]
  tranr15 = Resistor [tolerance=±5% resistance=1k package=THT]
  tranr16 = Resistor [tolerance=±5% resistance=1k package=THT]
  tranr17 = Resistor [tolerance=±5% resistance=1k package=THT]
  midioptocoupler = 6n137 [package="DIP8 [THT]"]
  d1 = Rectifier Diode [part_number=1N914 package="300 mil [THT]"]
  midiinout = DIN-5 jack (MIDI) [package=THT]
  midiinr2 = Resistor [tolerance=±5% resistance=470 package=THT]
  midiinr3 = Resistor [tolerance=±5% resistance=10k package=THT]
  midiinr1 = Resistor [tolerance=±5% resistance=220 package=THT]
  midioutr1 = Resistor [tolerance=±5% resistance=220 package=THT]
  midiswitch = Toggle Switch [package=THT]
  playstopbutt = Toggle Switch [package=THT]
  mutebutt = Toggle Switch [package=THT]
  LCD = LCD screen
  lcdpot = Rotary Potentiometer (Small) [maximum_resistance=100kΩ package=THT]
  lcdr = Resistor [tolerance=±5% resistance=220 package=THT]
  7segctrl = 74HC595 [package="DIP16 [THT]"]
  2n3904_(x2)_-_10 = MMDT3904 [package=sot363]
  2n3904_(x2)_-_11 = MMDT3904 [package=sot363]
  2n3904_(x2)_-_12 = MMDT3904 [package=sot363]
  2n3904_(x2)_-_13 = MMDT3904 [package=sot363]
  ledr17 = Resistor [tolerance=±5% resistance=2.2k package=THT]
  ledr18 = Resistor [tolerance=±5% resistance=2.2k package=THT]
  ledr19 = Resistor [tolerance=±5% resistance=2.2k package=THT]
  ledr20 = Resistor [tolerance=±5% resistance=2.2k package=THT]
  ledr21 = Resistor [tolerance=±5% resistance=2.2k package=THT]
  ledr22 = Resistor [tolerance=±5% resistance=2.2k package=THT]
  ledr23 = Resistor [tolerance=±5% resistance=2.2k package=THT]
  ledr24 = Resistor [tolerance=±5% resistance=2.2k package=THT]
  ledr25 = Resistor [tolerance=±5% resistance=2.2k package=THT]
  ledr26 = Resistor [tolerance=±5% resistance=2.2k package=THT]
  ledr27 = Resistor [tolerance=±5% resistance=2.2k package=THT]
  ledr28 = Resistor [tolerance=±5% resistance=2.2k package=THT]
  ledr29 = Resistor [tolerance=±5% resistance=2.2k package=THT]
  ledr30 = Resistor [tolerance=±5% resistance=2.2k package=THT]
  ledr31 = Resistor [tolerance=±5% resistance=2.2k package=THT]
  ledr32 = Resistor [tolerance=±5% resistance=2.2k package=THT]
  ledr33 = Resistor [tolerance=±5% resistance=2.2k package=THT]
  ledr34 = Resistor [tolerance=±5% resistance=2.2k package=THT]
  tranr18 = Resistor [tolerance=±5% resistance=1k package=THT]
  tranr19 = Resistor [tolerance=±5% resistance=1k package=THT]
  tranr20 = Resistor [tolerance=±5% resistance=1k package=THT]
  tranr21 = Resistor [tolerance=±5% resistance=1k package=THT]
  tranr22 = Resistor [tolerance=±5% resistance=1k package=THT]
  tranr23 = Resistor [tolerance=±5% resistance=1k package=THT]
  tranr24 = Resistor [tolerance=±5% resistance=1k package=THT]
  tranr25 = Resistor [tolerance=±5% resistance=1k package=THT]
  ledr7 = Resistor [tolerance=±5% resistance=470 package=THT]
  tranr18_2 = Resistor [tolerance=±5% resistance=1k package=THT]

nets:
  N1: seqledsctrl.Q1, tranr2.Pin_1
  N2: seqledsctrl.Q2, tranr3.Pin_1
  N3: seqledsctrl.Q3, tranr4.Pin_1
  N4: seqledsctrl.Q4, tranr5.Pin_1
  N5: seqledsctrl.Q5, tranr6.Pin_1
  N6: seqledsctrl.Q6, tranr7.Pin_1
  N7: seqledsctrl.Q7, tranr8.Pin_1
  GND: seqledsctrl.GND, seqledsctrl.OE, tempoledsctrl.GND, tempoledsctrl.OE, arduino_nano.GND, 2n3904_(x2)_-_1.G$2_E, 2n3904_(x2)_-_1.G$1_E, 2n3904_(x2)_-_2.G$2_E, 2n3904_(x2)_-_2.G$1_E, 2n3904_(x2)_-_3.G$2_E, 2n3904_(x2)_-_3.G$1_E, 2n3904_(x2)_-_4.G$2_E, 2n3904_(x2)_-_4.G$1_E, 2n3904_(x2)_-_5.G$2_E, 2n3904_(x2)_-_5.G$1_E, seqbutt1.L2, seqbutt2.L2, seqbutt3.L2, seqbutt4.L2, seqbutt8.L2, seqbutt5.L2, seqbutt6.L2, seqbutt7.L2, ctrlbutt1.L2, ctrlbutt2.L2, ctrlbutt3.L2, ctrlbutt4.L2, ctrlbutt5.L2, ctrlbutt6.L2, ctrlbutt7.L2, ctrlbutt8.L2, ctrlbutts.GND, seqbutts.GND, 2n3904_(x2)_-_6.G$2_E, 2n3904_(x2)_-_6.G$1_E, 2n3904_(x2)_-_7.G$2_E, 2n3904_(x2)_-_7.G$1_E, 2n3904_(x2)_-_8.G$2_E, 2n3904_(x2)_-_8.G$1_E, 2n3904_(x2)_-_9.G$2_E, 2n3904_(x2)_-_9.G$1_E, midioptocoupler.Pin_5, midiinout.2, midiinr3.Pin_0, playstopbutt.L2, mutebutt.L2, LCD.LED-, 7segctrl.GND, 7segctrl.OE, 2n3904_(x2)_-_10.G$2_E, 2n3904_(x2)_-_10.G$1_E, 2n3904_(x2)_-_11.G$2_E, 2n3904_(x2)_-_11.G$1_E, 2n3904_(x2)_-_12.G$2_E, 2n3904_(x2)_-_12.G$1_E, 2n3904_(x2)_-_13.G$2_E, 2n3904_(x2)_-_13.G$1_E
  N8: seqledsctrl.Q7', tempoledsctrl.DS
  5V: seqledsctrl.MR, seqledsctrl.VCC, tempoledsctrl.MR, tempoledsctrl.VCC, arduino_nano.5V, seqled1.common_anode, seqled2.common_anode, seqled3.common_anode, seqled4.common_anode, seqled5.common_anode, seqled6.common_anode, seqled7.common_anode, seqbutt1.L1, seqbutt2.L1, seqbutt3.L1, seqbutt4.L1, seqbutt8.L1, seqbutt5.L1, seqbutt6.L1, seqbutt7.L1, ctrlbutt1.L1, ctrlbutt2.L1, ctrlbutt3.L1, ctrlbutt4.L1, ctrlbutt5.L1, ctrlbutt6.L1, ctrlbutt7.L1, ctrlbutt8.L1, 7seg.common_anode, ctrlbutts.VCC, seqbutts.VCC, midioptocoupler.Pin_8, midiinr2.Pin_1, midioutr1.Pin_1, playstopbutt.L1, mutebutt.L1, LCD.VDD, lcdpot.leg2, lcdr.Pin_0, 7segctrl.MR, 7segctrl.VCC
  N9: seqledsctrl.SH_CP, tempoledsctrl.SH_CP, arduino_nano.D4, 7segctrl.SH_CP
  N10: seqledsctrl.ST_CP, tempoledsctrl.ST_CP, arduino_nano.D3, 7segctrl.ST_CP
  N11: seqledsctrl.DS, 7segctrl.Q7'
  N12: seqledsctrl.Q0, tranr1.Pin_1
  N13: tempoledsctrl.Q1, tranr24.Pin_1
  N14: tempoledsctrl.Q2, tranr23.Pin_1
  N15: tempoledsctrl.Q3, tranr22.Pin_1
  N16: tempoledsctrl.Q4, tranr21.Pin_1
  N17: tempoledsctrl.Q5, tranr20.Pin_1
  N18: tempoledsctrl.Q6, tranr19.Pin_1
  N19: tempoledsctrl.Q7, tranr18.Pin_1
  N20: tempoledsctrl.Q0, tranr25.Pin_1
  N21: arduino_nano.D1/TX, midiinout.5
  N22: arduino_nano.D0/RX, midiswitch.COM
  N23: arduino_nano.D2, 7segctrl.DS
  D5: arduino_nano.D5, tranr9.Pin_1
  D6: arduino_nano.D6
  D7: arduino_nano.D7, mutebutt.COM
  D8: arduino_nano.D8, playstopbutt.COM
  N24: arduino_nano.D9, ctrlbutts.CLK_INH, seqbutts.CLK_INH
  N25: arduino_nano.D10, seqbutts.QH
  N26: arduino_nano.D11/MOSI, ctrlbutts.SH/LD', seqbutts.SH/LD'
  N27: arduino_nano.D12/MISO, ctrlbutts.CLK, seqbutts.CLK
  N28: arduino_nano.A5, LCD.DB7
  N29: arduino_nano.A4, LCD.DB6
  N30: arduino_nano.A3, LCD.DB5
  N31: arduino_nano.A2, LCD.DB4
  N32: arduino_nano.A1, LCD.E
  N33: arduino_nano.A0, LCD.RS
  3.3V: arduino_nano.3V3
  N34: 2n3904_(x2)_-_1.G$2_B, tranr1.Pin_0
  N35: 2n3904_(x2)_-_1.G$1_C, ledr23.Pin_0
  N36: 2n3904_(x2)_-_1.G$1_B, tranr2.Pin_0
  N37: 2n3904_(x2)_-_1.G$2_C, ledr24.Pin_0
  N38: 2n3904_(x2)_-_2.G$2_B, tranr3.Pin_0
  N39: 2n3904_(x2)_-_2.G$1_C, ledr21.Pin_0
  N40: 2n3904_(x2)_-_2.G$1_B, tranr4.Pin_0
  N41: 2n3904_(x2)_-_2.G$2_C, ledr22.Pin_0
  N42: 2n3904_(x2)_-_3.G$2_B, tranr5.Pin_0
  N43: 2n3904_(x2)_-_3.G$1_C, ledr19.Pin_0
  N44: 2n3904_(x2)_-_3.G$1_B, tranr6.Pin_0
  N45: 2n3904_(x2)_-_3.G$2_C, ledr20.Pin_0
  N46: 2n3904_(x2)_-_4.G$2_B, tranr7.Pin_0
  N47: 2n3904_(x2)_-_4.G$1_C, ledr17.Pin_0
  N48: 2n3904_(x2)_-_4.G$1_B, tranr8.Pin_0
  N49: 2n3904_(x2)_-_4.G$2_C, ledr18.Pin_0
  N50: 2n3904_(x2)_-_5.G$2_B, tranr9.Pin_0
  N51: 2n3904_(x2)_-_5.G$1_C, ledr33.Pin_0
  N52: 2n3904_(x2)_-_5.G$1_B, tranr10.Pin_0
  N53: 2n3904_(x2)_-_5.G$2_C, ledr34.Pin_0
  N54: seqled1.blue_cathode, ledr32.Pin_1
  N55: seqled1.green_cathode, ledr24.Pin_1
  N56: seqled2.blue_cathode, ledr31.Pin_1
  N57: seqled2.green_cathode, ledr23.Pin_1
  N58: seqled3.blue_cathode, ledr30.Pin_1
  N59: seqled3.green_cathode, ledr22.Pin_1
  N60: seqled4.blue_cathode, ledr29.Pin_1
  N61: seqled4.green_cathode, ledr21.Pin_1
  N62: seqled5.blue_cathode, ledr28.Pin_1
  N63: seqled5.green_cathode, ledr20.Pin_1
  N64: seqled6.blue_cathode, ledr27.Pin_1
  N65: seqled6.green_cathode, ledr19.Pin_1
  N66: seqled7.blue_cathode, ledr26.Pin_1
  N67: seqled7.green_cathode, ledr18.Pin_1
  N68: seqled8.common_anode, playstopled.anode, muteled.anode
  N69: seqled8.blue_cathode, ledr25.Pin_1
  N70: seqled8.green_cathode, ledr17.Pin_1
  N71: playstopled.cathode, ledr34.Pin_1
  N72: muteled.cathode, ledr33.Pin_1
  N73: seqbutt1.COM, seqbutts.A
  N74: seqbutt2.COM, seqbutts.B
  N75: seqbutt3.COM, seqbutts.C
  N76: seqbutt4.COM, seqbutts.D
  N77: seqbutt8.COM, seqbutts.H
  N78: seqbutt5.COM, seqbutts.E
  N79: seqbutt6.COM, seqbutts.F
  N80: seqbutt7.COM, seqbutts.G
  N81: ctrlbutt1.COM, ctrlbutts.A
  N82: ctrlbutt2.COM, ctrlbutts.B
  N83: ctrlbutt3.COM, ctrlbutts.C
  N84: ctrlbutt4.COM, ctrlbutts.D
  N85: ctrlbutt5.COM, ctrlbutts.E
  N86: ctrlbutt6.COM, ctrlbutts.F
  N87: ctrlbutt7.COM, ctrlbutts.G
  N88: ctrlbutt8.COM, ctrlbutts.H
  N89: 7seg.Segment_E, ledr14.Pin_1
  N90: 7seg.Segment_D, ledr13.Pin_1
  N91: 7seg.Segment_C, ledr12.Pin_1
  N92: 7seg.Segment_DP, ledr7.Pin_1
  N93: 7seg.Segment_B, ledr11.Pin_1
  N94: 7seg.Segment_A, 7segr1.Pin_1
  N95: 7seg.Segment_F, ledr15.Pin_1
  N96: 7seg.Segment_G, ledr16.Pin_1
  d6: tranr10.Pin_1
  N97: ctrlbutts.QH, seqbutts.SER
  N98: 7segr1.Pin_0, 2n3904_(x2)_-_6.G$2_C
  N99: ledr11.Pin_0, 2n3904_(x2)_-_6.G$1_C
  N100: ledr12.Pin_0, 2n3904_(x2)_-_7.G$2_C
  N101: ledr13.Pin_0, 2n3904_(x2)_-_7.G$1_C
  N102: ledr14.Pin_0, 2n3904_(x2)_-_8.G$2_C
  N103: ledr15.Pin_0, 2n3904_(x2)_-_8.G$1_C
  N104: ledr16.Pin_0, 2n3904_(x2)_-_9.G$2_C
  N105: 2n3904_(x2)_-_6.G$2_B, tranr11.Pin_0
  N106: 2n3904_(x2)_-_6.G$1_B, tranr12.Pin_0
  N107: 2n3904_(x2)_-_7.G$2_B, tranr13.Pin_0
  N108: 2n3904_(x2)_-_7.G$1_B, tranr14.Pin_0
  N109: 2n3904_(x2)_-_8.G$2_B, tranr15.Pin_0
  N110: 2n3904_(x2)_-_8.G$1_B, tranr16.Pin_0
  N111: 2n3904_(x2)_-_9.G$2_B, tranr17.Pin_0
  N112: 2n3904_(x2)_-_9.G$1_C, ledr7.Pin_0
  N113: 2n3904_(x2)_-_9.G$1_B, tranr18_2.Pin_0
  N114: tranr11.Pin_1, 7segctrl.Q0
  N115: tranr12.Pin_1, 7segctrl.Q1
  N116: tranr13.Pin_1, 7segctrl.Q2
  N117: tranr14.Pin_1, 7segctrl.Q3
  N118: tranr15.Pin_1, 7segctrl.Q4
  N119: tranr16.Pin_1, 7segctrl.Q5
  N120: tranr17.Pin_1, 7segctrl.Q6
  N121: midioptocoupler.Pin_2, d1.cathode, midiinr1.Pin_0
  N122: midioptocoupler.Pin_3, d1.anode, midiinout.3
  N123: midioptocoupler.Pin_6, midiinr2.Pin_0, midiswitch.L2
  N124: midioptocoupler.Pin_7, midiinr3.Pin_1
  N125: midiinout.4, midioutr1.Pin_0
  N126: midiinout.1, midiinr1.Pin_1
  N127: LCD.VSS, LCD.R/W, lcdpot.leg1
  N128: LCD.V0, lcdpot.wiper
  N129: LCD.LED+, lcdr.Pin_1
  N130: 7segctrl.Q7, tranr18_2.Pin_1
  N131: 2n3904_(x2)_-_10.G$2_B, tranr19.Pin_0
  N132: 2n3904_(x2)_-_10.G$1_C, ledr25.Pin_0
  N133: 2n3904_(x2)_-_10.G$1_B, tranr18.Pin_0
  N134: 2n3904_(x2)_-_10.G$2_C, ledr26.Pin_0
  N135: 2n3904_(x2)_-_11.G$2_B, tranr21.Pin_0
  N136: 2n3904_(x2)_-_11.G$1_C, ledr27.Pin_0
  N137: 2n3904_(x2)_-_11.G$1_B, tranr20.Pin_0
  N138: 2n3904_(x2)_-_11.G$2_C, ledr28.Pin_0
  N139: 2n3904_(x2)_-_12.G$2_B, tranr23.Pin_0
  N140: 2n3904_(x2)_-_12.G$1_C, ledr29.Pin_0
  N141: 2n3904_(x2)_-_12.G$1_B, tranr22.Pin_0
  N142: 2n3904_(x2)_-_12.G$2_C, ledr30.Pin_0
  N143: 2n3904_(x2)_-_13.G$2_B, tranr25.Pin_0
  N144: 2n3904_(x2)_-_13.G$1_C, ledr31.Pin_0
  N145: 2n3904_(x2)_-_13.G$1_B, tranr24.Pin_0
  N146: 2n3904_(x2)_-_13.G$2_C, ledr32.Pin_0

notes:
  MIDI IN OUT
  7 SEGMENT DISPLAY (VOICE NUMBER)
  SEQUENCER LEDS
  SEQUENCER & CONTROL BUTTONS
  LCD

custom parts:
  74HC165: 8-bit parallel-load shift registers
  6n137: Opto coupler
