# Fritzing sketch synth (saved by Fritzing 0.9.3b)

parts:
  arduino_due = Arduino Due (Rev2b)
  midioptocoupler1 = 6n137 [package="DIP8 [THT]"]
  d2 = Rectifier Diode [part_number=1N914 package="300 mil [THT]"]
  midiinout1 = DIN-5 jack (MIDI) [package=THT]
  midiinr4 = Resistor [tolerance=±5% resistance=470 package=THT]
  midiinr5 = Resistor [tolerance=±5% resistance=10k package=THT]
  midiinr6 = Resistor [tolerance=±5% resistance=220 package=THT]
  midioutr2 = Resistor [tolerance=±5% resistance=220 package=THT]
  midioptocoupler2 = 6n137 [package="DIP8 [THT]"]
  d3 = Rectifier Diode [part_number=1N914 package="300 mil [THT]"]
  midiinout2 = DIN-5 jack (MIDI) [package=THT]
  midiinr7 = Resistor [tolerance=±5% resistance=470 package=THT]
  midiinr8 = Resistor [tolerance=±5% resistance=10k package=THT]
  midiinr9 = Resistor [tolerance=±5% resistance=220 package=THT]
  midioutr3 = Resistor [tolerance=±5% resistance=220 package=THT]
  midioptocoupler3 = 6n137 [package="DIP8 [THT]"]
  d4 = Rectifier Diode [part_number=1N914 package="300 mil [THT]"]
  midiinout3 = DIN-5 jack (MIDI) [package=THT]
  midiinr10 = Resistor [tolerance=±5% resistance=470 package=THT]
  midiinr11 = Resistor [tolerance=±5% resistance=10k package=THT]
  midiinr12 = Resistor [tolerance=±5% resistance=220 package=THT]
  midioutr4 = Resistor [tolerance=±5% resistance=220 package=THT]
  midioptocoupler4 = 6n137 [package="DIP8 [THT]"]
  d5 = Rectifier Diode [part_number=1N914 package="300 mil [THT]"]
  midiinout4 = DIN-5 jack (MIDI) [package=THT]
  midiinr13 = Resistor [tolerance=±5% resistance=470 package=THT]
  midiinr14 = Resistor [tolerance=±5% resistance=10k package=THT]
  midiinr15 = Resistor [tolerance=±5% resistance=220 package=THT]
  midioutr5 = Resistor [tolerance=±5% resistance=220 package=THT]
  midiswitch = Toggle Switch [package=THT]
  menuctrlbutt1 = Toggle Switch [package=THT]
  menuctrlbutt2 = Toggle Switch [package=THT]
  LCD = LCD screen
  audiooutr2 = Resistor [tolerance=±5% resistance=470 package=THT]
  audiooutr1 = Resistor [tolerance=±5% resistance=470 package=THT]
  ring = female pin header, 1 pin [form="♀ (female)"]
  tip = female pin header, 1 pin [form="♀ (female)"]
  sleeve = female pin header, 1 pin [form="♀ (female)"]
  rotenc = ENCODER-QUADRATURE [package=encoder-16mm-quad]
  lcdpot = Rotary Potentiometer (Small) [maximum_resistance=100kΩ package=THT]
  lcdr = Resistor [tolerance=±5% resistance=220 package=THT]

nets:
  N1: arduino_due.DAC0, audiooutr1.Pin_0
  N2: arduino_due.DAC1, audiooutr2.Pin_0
  N3: arduino_due.D14/TX3, midiinout3.5
  N4: arduino_due.D15/RX3, midioptocoupler3.Pin_6, midiinr10.Pin_0
  N5: arduino_due.D16/TX2, midiinout2.5
  N6: arduino_due.D17/RX2, midioptocoupler2.Pin_6, midiinr7.Pin_0
  N7: arduino_due.D18/TX1, midiinout1.5
  N8: arduino_due.D19/RX1, midioptocoupler1.Pin_6, midiinr4.Pin_0
  N9: arduino_due.D0/RX, midiswitch.COM
  N10: arduino_due.D1/TX, midiinout4.5
  N11: arduino_due.D22, menuctrlbutt1.COM
  N12: arduino_due.D23, menuctrlbutt2.COM
  N13: arduino_due.D40, LCD.RS
  N14: arduino_due.D41, LCD.E
  N15: arduino_due.D42, LCD.DB4
  N16: arduino_due.D43, LCD.DB5
  N17: arduino_due.D44, LCD.DB6
  N18: arduino_due.D45, LCD.DB7
  N19: arduino_due.D52, rotenc.A
  N20: arduino_due.D53, rotenc.B
  N21: midioptocoupler1.Pin_2, d2.cathode, midiinr6.Pin_0
  N22: midioptocoupler1.Pin_3, d2.anode, midiinout1.3
  GND: midioptocoupler1.Pin_5, midiinout1.2, midiinr5.Pin_0, midioptocoupler2.Pin_5, midiinout2.2, midiinr8.Pin_0, midioptocoupler3.Pin_5, midiinout3.2, midiinr11.Pin_0, midioptocoupler4.Pin_5, midiinout4.2, midiinr14.Pin_0, menuctrlbutt1.L2, menuctrlbutt2.L2, LCD.VSS, LCD.R/W, LCD.LED-, sleeve.pin1, rotenc.C, lcdpot.leg1
  N23: midioptocoupler1.Pin_7, midiinr5.Pin_1
  3.3V: midioptocoupler1.Pin_8, midiinr4.Pin_1, midioutr2.Pin_1, midioptocoupler2.Pin_8, midiinr7.Pin_1, midioutr3.Pin_1, midioptocoupler3.Pin_8, midiinr10.Pin_1, midioutr4.Pin_1, midioptocoupler4.Pin_8, midiinr13.Pin_1, midioutr5.Pin_1
  N24: midiinout1.4, midioutr2.Pin_0
  N25: midiinout1.1, midiinr6.Pin_1
  N26: midioptocoupler2.Pin_2, d3.cathode, midiinr9.Pin_0
  N27: midioptocoupler2.Pin_3, d3.anode, midiinout2.3
  N28: midioptocoupler2.Pin_7, midiinr8.Pin_1
  N29: midiinout2.4, midioutr3.Pin_0
  N30: midiinout2.1, midiinr9.Pin_1
  N31: midioptocoupler3.Pin_2, d4.cathode, midiinr12.Pin_0
  N32: midioptocoupler3.Pin_3, d4.anode, midiinout3.3
  N33: midioptocoupler3.Pin_7, midiinr11.Pin_1
  N34: midiinout3.4, midioutr4.Pin_0
  N35: midiinout3.1, midiinr12.Pin_1
  N36: midioptocoupler4.Pin_2, d5.cathode, midiinr15.Pin_0
  N37: midioptocoupler4.Pin_3, d5.anode, midiinout4.3
  N38: midioptocoupler4.Pin_6, midiinr13.Pin_0
  N39: midioptocoupler4.Pin_7, midiinr14.Pin_1
  N40: midiinout4.4, midioutr5.Pin_0
  N41: midiinout4.1, midiinr15.Pin_1
  5V: menuctrlbutt1.L1, menuctrlbutt2.L1, LCD.VDD, lcdpot.leg2, lcdr.Pin_0
  N42: LCD.V0, lcdpot.wiper
  N43: LCD.LED+, lcdr.Pin_1
  N44: audiooutr2.Pin_1, ring.pin1
  N45: audiooutr1.Pin_1, tip.pin1

notes:
  AUDIO OUT
  MENU CONTROL
  MIDI IN OUT (4x)
  LCD

custom parts:
  6n137: Opto coupler
